# Fritzing sketch Anemometro_IoT_LoRaWAN (saved by Fritzing 0.9.10b)

parts:
  12V_DC_to_3_3V_DC = DC_DC_XL4016 [package=board_screw]
  Mod2 = Heltec CubeCell Dev-Board [part_number=HTCC-AB01]
  12V_DC = 2.1mm Barrel Jack with Terminal Block
  M3 = Adafruit Anemometer [package=THT]

nets:
  N1: 12V_DC_to_3_3V_DC.IN+, 12V_DC.POS, M3.pin1
  N2: 12V_DC_to_3_3V_DC.IN-, 12V_DC.NEG
  N3: 12V_DC_to_3_3V_DC.OUT-, Mod2.pin_11, Mod2.pin_14, M3.pin2
  N4: Mod2.pin1, M3.pin3

custom parts:
  Heltec CubeCell Dev-Board: CubeCell is a part of the Heltec LoRa series and incorporates a PSoC 4000 series processor and SX1262 RF transceiver with an integrated CP2102 USB to serial port interface and onboard SHT1.25 battery interface with integrated lithium battery management system, supporting direct solar panel connection. Links: Heltec CubeCell Dev-Board product page Github
  Adafruit Anemometer: Adafruit Anemometer Wind Speed Sensor w/Analog Voltage Output.
