# Fritzing sketch anemometro_arduino_knx (saved by Fritzing 0.9.3b)

parts:
  12V_Battery = Lilypad Battery Connect
  M1 = Adafruit Anemometer [package=THT]
  Part1 = Arduino Uno (Rev3) - ICSP
  LCD_16X2 = LCD-16X2 [package=lcd-16x2_nosilk]
  LED1 = smd LED [color="Red (633nm)" package="0603 [SMD]"]
  LED2 = smd LED [color="Green (570nm)" package="0603 [SMD]"]
  S1 = Pushbutton [package="[SMD]"]
  R1 = Resistor [tolerance=±5% resistance=220 package="0603 [SMD]"]
  R2 = Resistor [tolerance=±5% resistance=220 package="0603 [SMD]"]
  R3 = Resistor [tolerance=±5% resistance=10k package="0805 [SMD]"]

nets:
  N1: 12V_Battery.-, M1.pin2, Part1.GND, LCD_16X2.DB6, LED1.cathode, LED2.cathode, S1.Pin_3, S1.Pin_4, R3.Pin_1
  N2: 12V_Battery.+, M1.pin1
  N3: M1.pin3, Part1.A0
  N4: Part1.A4/SDA, LCD_16X2.A
  N5: Part1.A5/SCL, LCD_16X2.K
  N6: Part1.D13/SCK, R2.Pin_0
  N7: Part1.D2, R3.Pin_0
  N8: Part1.D7, R1.Pin_0
  N9: Part1.5V, LCD_16X2.DB5
  N10: LED1.anode, R1.Pin_1
  N11: LED2.anode, R2.Pin_1

notes:
  MAX3232

custom parts:
  Adafruit Anemometer: Adafruit Anemometer Wind Speed Sensor w/Analog Voltage Output.
