# Fritzing sketch anemometro_arduino_wifi_mqtt_SolidState (saved by Fritzing 0.9.10b)

parts:
  WeMos_D1_Mini2 = WeMos D1 Mini
  -_+_Tx_Rx = Header 4 [package=molex-1x4_lock]

nets:
  N1: WeMos_D1_Mini2.3V3, -_+_Tx_Rx.2
  N2: WeMos_D1_Mini2.G, -_+_Tx_Rx.1
  N3: WeMos_D1_Mini2.RX, -_+_Tx_Rx.4
  N4: WeMos_D1_Mini2.TX, -_+_Tx_Rx.3
