# Fritzing sketch anemometro_arduino_wifi_mqtt_SolidState (saved by Fritzing 0.9.10b)

parts:
  WeMos_D1_Mini2 = WeMos D1 Mini
  C_|_Tx_|_Rx_|_+_|_- = Header 5 [package=1x05-1mm]
  DC_5V = Power Jack [package=power_jack_smd]

nets:
  N1: WeMos_D1_Mini2.5V, C_|_Tx_|_Rx_|_+_|_-.4, DC_5V.PWR
  N2: WeMos_D1_Mini2.G, C_|_Tx_|_Rx_|_+_|_-.5, DC_5V.GND
  N3: WeMos_D1_Mini2.RX, C_|_Tx_|_Rx_|_+_|_-.3
  N4: WeMos_D1_Mini2.TX, C_|_Tx_|_Rx_|_+_|_-.2
