# Fritzing sketch anemometro_rpi_ethernet_mqtt (saved by Fritzing 0.9.10b)

parts:
  Raspberry_Pi1 = Raspberry Pi 2
  12V_Battery1 = Lilypad Battery Connect  # not connected
  M2 = Adafruit Anemometer [package=THT]

nets:
  N1: Raspberry_Pi1.GND, M2.pin2
  N2: Raspberry_Pi1.GPIO23, M2.pin3

custom parts:
  Adafruit Anemometer: Adafruit Anemometer Wind Speed Sensor w/Analog Voltage Output.
